# Fritzing sketch car_stable_1 (saved by Fritzing 0.9.3b)
breadboards: 1

parts:
  Часть1 = Arduino Uno (Rev3) - ICSP
  Часть2 = NRF24L01+ Breakout Board
  U1 = L298 [package=multiwatt15]
  hc-sr1 = hc-sr04
  M1 = DC Motor  # not connected
  M2 = DC Motor  # not connected
  M3 = DC Motor  # not connected
  M4 = DC Motor  # not connected
  VCC1 = Battery block 9V  # not connected
  U2 = LIPO-2000mAh [package=lipo-2000]

nets:
  N1: Часть1.ICSP_MISO, Часть1.D12/MISO, Часть2.MISO
  N2: Часть1.D8, Часть2.CE
  N3: Часть1.D9_PWM, U1.ENB
  N4: Часть1.D10_PWM/SS, Часть2.CS
  N5: Часть1.D11_PWM/MOSI, Часть2.MOSI
  N6: Часть1.D13/SCK, Часть2.SCK
  GND: Часть1.GND, hc-sr1.GND
  N7: Часть1.D1/TX, hc-sr1.Echo
  N8: Часть1.D2, hc-sr1.Trig
  N9: Часть1.D3_PWM, U1.ENA
  N10: Часть1.D4, U1.IN1
  N11: Часть1.D5_PWM, U1.IN2
  N12: Часть1.D6_PWM, U1.IN3
  N13: Часть1.D7, U1.IN4
  5V: Часть1.5V, hc-sr1.VCC
  N14: Часть2.VCC, U1.VLS
  N15: U1.VS, U2.+
  N16: U1.GND, U2.-
