# Fritzing sketch hand_stable_1 (saved by Fritzing 0.9.3b)

parts:
  Часть1 = NRF24L01+ Breakout Board
  Часть3 = Arduino Nano (Rev3.0)
  Часть5 = Tri-Axis Gyro Breakout - L3G4200D
  VCC1 = Battery block 9V

nets:
  GND: Часть1.GND, Часть3.GND, VCC1.-
  VCC: Часть1.VCC, Часть3.RESET, Часть3.5V
  N1: Часть1.CE, Часть3.D9
  N2: Часть1.CS, Часть3.D10
  N3: Часть1.SCK, Часть3.D13/SCK
  N4: Часть1.MOSI, Часть1.MISO, Часть3.D11/MOSI, Часть3.D12/MISO
  N5: Часть3.VIN, VCC1.+
  N6: Часть3.A5, Часть5.SCL
  N7: Часть3.A4, Часть5.SDA
  3V3: Часть3.3V3, Часть5.VCC
